# Fritzing sketch MKRFOX1200_mobile-weather-station_Breadboard (saved by Fritzing 0.9.3b)

parts:
  MKRFox1 = Arduino MKR Fox 1200
  PART1 = ML8511 UV Sensor Breakout [part_number=SEN-12705]
  Part1 = Adafruit BMP180
  U1 = LIPO-110mAh [package=lipo-110]  # not connected
  ANT1 = Antenna  # not connected

nets:
  GND: MKRFox1.GND, PART1.GND, Part1.GND
  N1: MKRFox1.A1, PART1.OUT
  VCC: MKRFox1.A2, MKRFox1.VCC, PART1.EN, PART1.3.3V, Part1.+3V3
  N2: MKRFox1.12/SCL, Part1.SCL
  N3: MKRFox1.11/SDA, Part1.SDA

custom parts:
  ML8511 UV Sensor Breakout: Description: The ML8511 breakout is an easy to use ultraviolet light sensor. The MP8511 UV Sensor works by outputing an analog signal in relation to the amount of UV light it detects. This breakout can be very handy in creating devices that warn the user of sunburn or detect the UV index as it relates to weather conditions. This sensor breakout can detect 280-390nm light most effectively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
  Adafruit BMP180: This precision sensor from Bosch is the best low-cost sensing solution for measuring barometric pressure and temperature. Because pressure changes with altitude you can also use it as an altimeter! The sensor is soldered onto a PCB with a 3.3V regulator, I2C level shifter and pull-up resistors on the I2C pins. The BMP180 is the next-generation of sensors from Bosch, and replaces the BMP085.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
